// Logisim project circuit1a.circ as structural Verilog: 1 circuit, main circuit main
module main (
  input  A,
  input  B,
  input  C,
  output result
);

  wire AandnotC_out, AxorBC_out, BC_out, not_1_out, not_2_out, not_C_and_B_out, xor_1_out;

  not not_1 (not_1_out, C);
  not not_2 (not_2_out, C);
  and BC (BC_out, B, C);
  and not_C_and_B (not_C_and_B_out, B, not_2_out);
  and AandnotC (AandnotC_out, not_1_out, A);
  xor AxorBC (AxorBC_out, A, BC_out);
  xor xor_1 (xor_1_out, AxorBC_out, not_C_and_B_out);
  or or_1 (result, AandnotC_out, xor_1_out);
endmodule
