// Logisim project circuit1c.circ as structural Verilog: 1 circuit, main circuit main
module main (
  input  A,
  input  B,
  input  C,
  output result
);

  wire BandC_out, left_out, not_1_out, not_2_out, not_3_out, not_4_out, notBandNotC_out, or_1_out, right_out;

  not not_1 (not_1_out, C);
  not not_2 (not_2_out, A);
  and left (left_out, not_1_out, not_2_out);
  not not_3 (not_3_out, B);
  and notBandNotC (notBandNotC_out, not_3_out, not_4_out);
  not not_4 (not_4_out, C);
  and BandC (BandC_out, B, C);
  or or_1 (or_1_out, notBandNotC_out, BandC_out);
  and right (right_out, A, or_1_out);
  or leftORright (result, left_out, right_out);
endmodule
