// Logisim project my_adder.circ as structural Verilog: 2 circuits, main circuit main
module main (
  input  sub,
  input  [15:0] B,
  input  [15:0] A,
  output [15:0] result,
  output ovf
);

  wire CO0, CO1, CO2, CO3, CO4, CO5, CO6, CO7, CO8, CO9, CO10, CO11, CO12, CO13, CO14, fifteen_cout,
       xor_1_out, xor_2_out, xor_3_out, xor_4_out, xor_5_out, xor_6_out, xor_7_out, xor_8_out, xor_9_out,
       xor_10_out, xor_11_out, xor_12_out, xor_13_out, xor_14_out, xor_15_out, xor_16_out;

  xor overflow (ovf, CO14, fifteen_cout);
  fullAdder fifteen (.Cin(CO14), .A(xor_1_out), .B(A[15]), .Sum(result[15]), .Cout(fifteen_cout));
  xor xor_1 (xor_1_out, sub, B[15]);
  fullAdder fourteen (.Cin(CO13), .A(xor_2_out), .B(A[14]), .Sum(result[14]), .Cout(CO14));
  xor xor_2 (xor_2_out, sub, B[14]);
  fullAdder thirteen (.Cin(CO12), .A(xor_3_out), .B(A[13]), .Sum(result[13]), .Cout(CO13));
  xor xor_3 (xor_3_out, sub, B[13]);
  fullAdder twelve (.Cin(CO11), .A(xor_4_out), .B(A[12]), .Sum(result[12]), .Cout(CO12));
  xor xor_4 (xor_4_out, sub, B[12]);
  fullAdder eleven (.Cin(CO10), .A(xor_5_out), .B(A[11]), .Sum(result[11]), .Cout(CO11));
  xor xor_5 (xor_5_out, sub, B[11]);
  fullAdder ten (.Cin(CO9), .A(xor_6_out), .B(A[10]), .Sum(result[10]), .Cout(CO10));
  xor xor_6 (xor_6_out, sub, B[10]);
  fullAdder nine (.Cin(CO8), .A(xor_7_out), .B(A[9]), .Sum(result[9]), .Cout(CO9));
  xor xor_7 (xor_7_out, sub, B[9]);
  fullAdder eight (.Cin(CO7), .A(xor_8_out), .B(A[8]), .Sum(result[8]), .Cout(CO8));
  xor xor_8 (xor_8_out, sub, B[8]);
  fullAdder seven (.Cin(CO6), .A(xor_9_out), .B(A[7]), .Sum(result[7]), .Cout(CO7));
  xor xor_9 (xor_9_out, sub, B[7]);
  fullAdder six (.Cin(CO5), .A(xor_10_out), .B(A[6]), .Sum(result[6]), .Cout(CO6));
  xor xor_10 (xor_10_out, sub, B[6]);
  fullAdder five (.Cin(CO4), .A(xor_11_out), .B(A[5]), .Sum(result[5]), .Cout(CO5));
  xor xor_11 (xor_11_out, sub, B[5]);
  fullAdder four (.Cin(CO3), .A(xor_12_out), .B(A[4]), .Sum(result[4]), .Cout(CO4));
  xor xor_12 (xor_12_out, sub, B[4]);
  fullAdder three (.Cin(CO2), .A(xor_13_out), .B(A[3]), .Sum(result[3]), .Cout(CO3));
  xor xor_13 (xor_13_out, sub, B[3]);
  fullAdder two (.Cin(CO1), .A(xor_14_out), .B(A[2]), .Sum(result[2]), .Cout(CO2));
  xor xor_14 (xor_14_out, sub, B[2]);
  fullAdder one (.Cin(CO0), .A(xor_15_out), .B(A[1]), .Sum(result[1]), .Cout(CO1));
  xor xor_15 (xor_15_out, sub, B[1]);
  fullAdder zero (.Cin(sub), .A(xor_16_out), .B(A[0]), .Sum(result[0]), .Cout(CO0));
  xor xor_16 (xor_16_out, sub, B[0]);

  // Other names for the same wires on the sheet: S0 = result[0]; S1 = result[1]; S2 = result[2]; S3 = result[3];
  //   S4 = result[4]; S5 = result[5]; S6 = result[6]; S7 = result[7]; S8 = result[8]; S9 = result[9];
  //   S10 = result[10]; S11 = result[11]; S12 = result[12]; S13 = result[13]; S14 = result[14]; S15 = result[15]
endmodule

module fullAdder (
  input  Cin,
  input  A,
  input  B,
  output Sum,
  output Cout
);

  wire and_1_out, and_2_out, xor_1_out;

  and and_1 (and_1_out, B, A);
  xor xor_1 (xor_1_out, A, B);
  or or_1 (Cout, and_1_out, and_2_out);
  and and_2 (and_2_out, xor_1_out, Cin);
  xor xor_2 (Sum, Cin, xor_1_out);
endmodule
