// Logisim project robot.circ as structural Verilog: 1 circuit, main circuit main
module main (
  input  [1:0] in_leftright,
  input  in_speed,
  output [1:0] out_position,
  output out_blocked
);

  wire c, d0, d0row1, d0row2, d0row3, d0row4, d1, d1row1, d1row2, d1row3, d1row4, d1row5, d1row6, d1row7,
       d1row8, d1row9, d1row10, d1row11, d1row12, d2, d2row1, d2row2, d2row3, d2row4, d2row5, d2row6, d2row7,
       d2row8, d2row9, d2row10, d2row11, d2row12, not_1_out, not_2_out, not_3_out, not_4_out, not_5_out,
       not_6_out, not_7_out, not_8_out, not_9_out, not_10_out, not_11_out, not_12_out, not_13_out,
       not_14_out, not_15_out, not_16_out, not_17_out, not_18_out, not_19_out, not_20_out, not_21_out,
       not_22_out, not_23_out, not_24_out, not_25_out, not_26_out, not_27_out, not_28_out, not_29_out,
       not_30_out, not_31_out, not_32_out, not_33_out, not_34_out, not_35_out, not_36_out, not_37_out,
       not_38_out, not_39_out, not_40_out, not_41_out, not_42_out, not_43_out, not_44_out, not_45_out,
       not_46_out, not_47_out, not_48_out, not_49_out, not_50_out, not_51_out, not_52_out, not_53_out,
       not_54_out, not_55_out, not_56_out, not_57_out, not_58_out, not_59_out, not_60_out, not_61_out,
       not_62_out, not_63_out, not_64_out, not_65_out, not_66_out, not_67_out, not_68_out, not_69_out,
       not_70_out, not_71_out, not_72_out, not_73_out, not_74_out, not_75_out, not_76_out, not_77_out,
       not_78_out;

  not not_1 (not_1_out, out_position[1]);
  not not_2 (not_2_out, out_position[0]);
  not not_3 (not_3_out, out_blocked);
  not not_4 (not_4_out, in_leftright[0]);
  not not_5 (not_5_out, in_speed);
  not not_6 (not_6_out, out_position[0]);
  not not_7 (not_7_out, out_blocked);
  not not_8 (not_8_out, in_leftright[1]);
  not not_9 (not_9_out, in_speed);
  not not_10 (not_10_out, out_blocked);
  not not_11 (not_11_out, in_leftright[0]);
  and and_1 (d2row1, not_18_out, not_19_out, not_20_out, in_leftright[1], not_21_out, in_speed);
  and and_2 (d2row5, out_position[1], not_22_out, not_23_out, not_24_out, not_25_out);
  and and_3 (d2row9, out_position[1], out_position[0], not_26_out, in_leftright[1], not_27_out);
  Clock clock_1 (.out(c));
  not not_12 (not_12_out, out_position[1]);
  not not_13 (not_13_out, out_position[0]);
  not not_14 (not_14_out, out_blocked);
  not not_15 (not_15_out, in_leftright[1]);
  not not_16 (not_16_out, out_blocked);
  not not_17 (not_17_out, in_leftright[0]);
  and and_4 (d0row3, out_position[1], out_position[0], not_16_out, in_leftright[1], not_17_out);
  and and_5 (d1row1, not_1_out, not_2_out, not_3_out, in_leftright[1], not_4_out, not_5_out);
  and and_6 (d1row5, out_position[1], not_6_out, not_7_out, not_8_out, in_leftright[0], not_9_out);
  and and_7 (d1row9, out_position[1], out_position[0], not_10_out, in_leftright[1], not_11_out);
  not not_18 (not_18_out, out_position[1]);
  not not_19 (not_19_out, out_position[0]);
  not not_20 (not_20_out, out_blocked);
  not not_21 (not_21_out, in_leftright[0]);
  not not_22 (not_22_out, out_position[0]);
  not not_23 (not_23_out, out_blocked);
  not not_24 (not_24_out, in_leftright[1]);
  not not_25 (not_25_out, in_leftright[0]);
  not not_26 (not_26_out, out_blocked);
  not not_27 (not_27_out, in_leftright[0]);
  and and_8 (d0row1, not_12_out, not_13_out, not_14_out, not_15_out, in_leftright[0]);
  D_Flip_Flop zero (.D(d0), .clk(c), .Q(out_blocked));  // open: Qn, preset, reset
  D_Flip_Flop one (.D(d1), .clk(c), .Q(out_position[0]));  // open: Qn, preset, reset
  D_Flip_Flop d_ff_1 (.D(d2), .clk(c), .Q(out_position[1]));  // open: Qn, preset, reset
  not not_28 (not_28_out, out_position[1]);
  not not_29 (not_29_out, out_position[0]);
  not not_30 (not_30_out, in_leftright[1]);
  not not_31 (not_31_out, in_leftright[0]);
  and and_9 (d2row2, not_41_out, not_42_out, out_blocked, in_leftright[1], not_43_out, in_speed);
  and and_10 (d2row6, out_position[1], not_44_out, not_45_out, in_leftright[1], not_46_out);
  and and_11 (d2row10, out_position[1], out_position[0], out_blocked, not_47_out, not_48_out);
  not not_32 (not_32_out, out_position[1]);
  not not_33 (not_33_out, out_position[0]);
  not not_34 (not_34_out, in_leftright[0]);
  not not_35 (not_35_out, in_speed);
  not not_36 (not_36_out, out_position[0]);
  not not_37 (not_37_out, out_blocked);
  not not_38 (not_38_out, in_leftright[0]);
  not not_39 (not_39_out, in_leftright[1]);
  not not_40 (not_40_out, in_leftright[0]);
  not not_41 (not_41_out, out_position[1]);
  not not_42 (not_42_out, out_position[0]);
  not not_43 (not_43_out, in_leftright[0]);
  not not_44 (not_44_out, out_position[0]);
  not not_45 (not_45_out, out_blocked);
  not not_46 (not_46_out, in_leftright[0]);
  not not_47 (not_47_out, in_leftright[1]);
  not not_48 (not_48_out, in_leftright[0]);
  and and_12 (d0row2, not_28_out, not_29_out, out_blocked, not_30_out, in_leftright[0]);
  and and_13 (d1row6, out_position[1], not_36_out, not_37_out, in_leftright[1], not_38_out);
  and and_14 (d1row10, out_position[1], out_position[0], out_blocked, not_39_out, not_40_out);
  and and_15 (d0row4, out_position[1], out_position[0], out_blocked, in_leftright[1], not_31_out);
  and and_16 (d1row2, not_32_out, not_33_out, out_blocked, in_leftright[1], not_34_out, not_35_out);
  and and_17 (d2row3, not_49_out, out_position[0], not_50_out, in_leftright[1], not_51_out, not_52_out);
  and and_18 (d2row7, out_position[1], out_position[0], not_53_out, not_54_out, not_55_out);
  and and_19 (d2row11, out_position[1], out_position[0], out_blocked, not_56_out, in_leftright[0], not_57_out);
  not not_49 (not_49_out, out_position[1]);
  not not_50 (not_50_out, out_blocked);
  not not_51 (not_51_out, in_leftright[0]);
  not not_52 (not_52_out, in_speed);
  not not_53 (not_53_out, out_blocked);
  not not_54 (not_54_out, in_leftright[1]);
  not not_55 (not_55_out, in_leftright[0]);
  not not_56 (not_56_out, in_leftright[1]);
  not not_57 (not_57_out, in_speed);
  not not_58 (not_58_out, out_position[1]);
  not not_59 (not_59_out, out_blocked);
  not not_60 (not_60_out, in_leftright[1]);
  not not_61 (not_61_out, in_leftright[0]);
  not not_62 (not_62_out, out_blocked);
  not not_63 (not_63_out, in_leftright[1]);
  not not_64 (not_64_out, in_leftright[0]);
  not not_65 (not_65_out, in_leftright[1]);
  or or_1 (d0, d0row1, d0row2, d0row3, d0row4);
  and and_20 (d1row7, out_position[1], out_position[0], not_62_out, not_63_out, not_64_out);
  and and_21 (d1row11, out_position[1], out_position[0], out_blocked, not_65_out, in_leftright[0], in_speed);
  and and_22 (d1row3, not_58_out, out_position[0], not_59_out, not_60_out, not_61_out);
  not not_66 (not_66_out, out_position[1]);
  not not_67 (not_67_out, out_blocked);
  and and_23 (d2row4, not_66_out, out_position[0], not_67_out, in_leftright[1], not_68_out, in_speed);
  not not_68 (not_68_out, in_leftright[0]);
  and and_24 (d2row8, out_position[1], out_position[0], not_69_out, not_70_out, in_leftright[0], not_71_out);
  and and_25 (d2row12, out_position[1], out_position[0], out_blocked, in_leftright[1], not_72_out);
  not not_69 (not_69_out, out_blocked);
  not not_70 (not_70_out, in_leftright[1]);
  not not_71 (not_71_out, in_speed);
  not not_72 (not_72_out, in_leftright[0]);
  or or_2 (d1, d1row1, d1row2, d1row3, d1row4, d1row5, d1row6, d1row7, d1row8, d1row9, d1row10, d1row11, d1row12);
  not not_73 (not_73_out, out_position[1]);
  not not_74 (not_74_out, out_blocked);
  not not_75 (not_75_out, in_leftright[0]);
  not not_76 (not_76_out, out_blocked);
  not not_77 (not_77_out, in_leftright[1]);
  not not_78 (not_78_out, in_leftright[0]);
  or or_3 (d2, d2row1, d2row2, d2row3, d2row4, d2row5, d2row6, d2row7, d2row8, d2row9, d2row10, d2row11, d2row12);
  and and_26 (d1row4, not_73_out, out_position[0], not_74_out, in_leftright[1], not_75_out, in_speed);
  and and_27 (d1row8, out_position[1], out_position[0], not_76_out, not_77_out, in_leftright[0], in_speed);
  and and_28 (d1row12, out_position[1], out_position[0], out_blocked, in_leftright[1], not_78_out);

  // Other names for the same wires on the sheet: in0 = in_leftright[0]; in1 = in_leftright[1]; Q1 = out_position[0];
  //   Q2 = out_position[1]; Q0 = out_blocked; speed = in_speed
endmodule
