// Logisim project cpu.circ as structural Verilog: 11 circuits, main circuit main
module main (
  input  reset
);

  wire and_1_out, and_2_out, beqz, blt, booleanShiftAmount, branchingPCplusB, clk, destination, inputaur,
       invert, jal, JalOrJ, jr, keyboard_1_avail, LoadOrStoreWord, lw, memory_latch_1_oe_latched,
       memory_latch_1_we_latched, multiplexer_4_out, notClock, NotOrShifting, or_2_out, outputaur,
       RS_is_zero, RSminusRTisNeg, RWE, sw, writeImmediate;
  wire [2:0] multiplexer_5_out, multiplexer_9_out, notRs, OPTYPE;
  wire [3:0] opcode;
  wire [6:0] KeyboardData;
  wire [7:7] LeaveSplitter;
  wire [11:0] address;
  wire [14:0] adding_2_result;
  wire [15:0] alu_1_outputdata, branchingVal, EnterPC, memory_latch_1_address_latched,
       memory_latch_1_data_in_latched, multiplexer_6_out, multiplexer_8_out, multiplexer_10_out, PC_dataout,
       PCplusBplus1_result, PcPlusOne, ProgramCounterRetain, ram_1_dout, reg1contents, reg2contents;

  Keyboard keyboard_1 (.clk(notClock), .re(inputaur), .clr(reset), .avail(keyboard_1_avail), .data(KeyboardData));
  Multiplexer #(.width(16), .enable("false")) multiplexer_1 (
    .in0(branchingVal), .in1(reg1contents), .out(ProgramCounterRetain), .sel(jr));
  Multiplexer #(.select(2), .width(16), .enable("false")) multiplexer_2 (
    .in0(branchingVal), .in1({4'b0000, address}), .in2(reg1contents), .out(EnterPC), .sel({jr, JalOrJ}));  // open: in3
  Adding adding_1 (.sub(1'b0), .B(16'h1), .A(PC_dataout), .result(PcPlusOne));  // open: ovf
  Adding PCplusBplus1 (
    .sub(1'b0), .B(PcPlusOne), .A({{11{address[5]}}, address[4:0]}), .result(PCplusBplus1_result));  // open: ovf
  Clock clock_1 (.out(clk));
  // Probe on keyboard_1_avail
  Multiplexer #(.width(16), .enable("false")) multiplexer_3 (
    .in0(PcPlusOne), .in1(PCplusBplus1_result), .out(branchingVal), .sel(branchingPCplusB));
  SingleRegister PC (.dataIn(EnterPC), .clk(notClock), .writeEnable(1'b1), .reset(reset), .dataOut(PC_dataout));
  not not_1 (notClock, clk);
  // Probe on KeyboardData
  ROM #(.addrWidth(16), .dataWidth(16)) rom_1 (.addr(PC_dataout), .data({opcode, address}));
  TTY #(.rows(13), .cols(80)) tty_1 (.data(reg1contents[6:0]), .clk(clk), .we(outputaur), .clr(reset));
  not not_2 (LeaveSplitter[7], keyboard_1_avail);
  // Probe on LeaveSplitter[7]
  Multiplexer #(.enable("false")) multiplexer_4 (.in0(1'b1), .in1(1'b0), .out(multiplexer_4_out), .sel(RWE));
  // Probe on 3'b111
  // Probe on address[5:3]
  Multiplexer #(.select(2), .width(3), .enable("false")) multiplexer_5 (
    .in0(address[5:3]), .in1(address[8:6]), .in2(3'b111), .out(multiplexer_5_out), .sel({jal, destination}));  // open: in3
  Multiplexer #(.select(2), .width(16), .enable("false")) multiplexer_6 (
    .in0(multiplexer_10_out), .in1(ProgramCounterRetain), .in2({{8{1'b0}}, LeaveSplitter[7], KeyboardData}),
    .out(multiplexer_6_out), .sel({inputaur, jal}));  // open: in3
  // Probe on address[5:0]
  Multiplexer #(.enable("false")) multiplexer_7 (.sel(jr));  // open: in0, in1, out
  not not_3 (notRs[1], address[10]);
  RegisterFile registerfile_1 (
    .clk(clk), .WriteData(multiplexer_6_out), .reset(reset), .RegWriteEnable(multiplexer_4_out),
    .WritePort(multiplexer_5_out), .ReadReg2(address[8:6]), .ReadReg1(address[11:9]),
    .Reg1Contents(reg1contents), .Reg2Contents(reg2contents));
  // Probe on reg2contents
  // Probe on multiplexer_8_out
  InstructionDecoder instructiondecoder_1 (
    .opcode(opcode), .RWE(destination), .destination(RWE), .ALUinput(OPTYPE),
    .ShiftAmount(booleanShiftAmount), .writeImmediate(writeImmediate), .NotOrShifting(NotOrShifting),
    .invert(invert), .StoreWord(sw), .LoadWord(lw), .LoadWordStoreWord(LoadOrStoreWord), .blt(blt),
    .beqz(beqz), .inputaur(inputaur), .outputaur(outputaur), .JalOrJ(JalOrJ), .jal(jal), .jr(jr));
  not not_4 (notRs[0], address[9]);
  not not_5 (notRs[2], address[11]);
  Multiplexer #(.select(2), .width(16), .enable("false")) multiplexer_8 (
    .in0(reg2contents), .in1({16{1'b0}}), .in2({{11{address[5]}}, address[4:0]}), .out(multiplexer_8_out),
    .sel({writeImmediate, NotOrShifting}));  // open: in3
  // Probe on address[11:9]
  // Probe on address[8:6]
  // Probe on address[5:3]
  // Probe on address[2:0]
  // Probe on reg1contents
  // Probe on notRs
  // Probe on OPTYPE
  Multiplexer #(.width(3), .enable("false")) multiplexer_9 (
    .in0(3'b000), .in1(address[2:0]), .out(multiplexer_9_out), .sel(booleanShiftAmount));
  // Probe on address[5:0]
  // Probe on address
  ALU alu_1 (
    .InputData1(reg1contents), .InputData2(multiplexer_8_out), .OpType(OPTYPE),
    .ShiftAmount(multiplexer_9_out), .OutputData(alu_1_outputdata));
  // Probe on multiplexer_8_out
  memory_latch memory_latch_1 (
    .address(alu_1_outputdata), .WE(sw), .clk(notClock), .data_in(reg2contents),
    .address_latched(memory_latch_1_address_latched), .WE_latched(memory_latch_1_we_latched),
    .OE_latched(memory_latch_1_oe_latched), .data_in_latched(memory_latch_1_data_in_latched));
  or or_1 (branchingPCplusB, and_1_out, and_2_out);
  and and_1 (and_1_out, RSminusRTisNeg, blt);
  and and_2 (and_2_out, RS_is_zero, beqz);
  or or_2 (or_2_out, reg1contents[0], reg1contents[1], reg1contents[2], reg1contents[3], reg1contents[4], reg1contents[5], reg1contents[6], reg1contents[7], reg1contents[9], reg1contents[10], reg1contents[11], reg1contents[12], reg1contents[13], reg1contents[8], reg1contents[15], reg1contents[14]);
  RAM #(.addrWidth(16), .dataWidth(16), .trigger("high"), .databus("bibus")) ram_1 (
    .addr(memory_latch_1_address_latched), .we(memory_latch_1_we_latched), .oe(memory_latch_1_oe_latched),
    .din(memory_latch_1_data_in_latched), .dout(ram_1_dout));
  Adding adding_2 (
    .sub(1'b1), .B(reg2contents), .A(reg1contents), .result({RSminusRTisNeg, adding_2_result}));  // open: ovf
  not not_6 (RS_is_zero, or_2_out);
  Multiplexer #(.width(16), .enable("false")) multiplexer_10 (
    .in0(alu_1_outputdata), .in1(ram_1_dout), .out(multiplexer_10_out), .sel(lw));
  // Probe on multiplexer_10_out

  // Other names for the same wires on the sheet: immediate[5:0] = address[5:0]; L[11:0] = address;
  //   ShiftAmount[2:0] = address[2:0]; SignExtendedImmediate[15:0] = {{11{address[5]}}, address[4:0]};
  //   zero = address[0]; one = address[1]; two = address[2]; Rd[2:0] = address[5:3]; three = address[3];
  //   four = address[4]; five = address[5]; Rt[2:0] = address[8:6]; six = address[6]; seven = address[7];
  //   eight = address[8]; nine = address[9]; Rs[2:0] = address[11:9]; ten = address[10]; eleven = address[11];
  //   LeaveSplitter[6:0] = KeyboardData

  // Notes on the sheet:
  //   contents of rom_1 (hex, n*v repeats v):
  //   205c 209a 3218 3420 42a8 4730 3c38 903f
endmodule

module SingleRegister (
  input  [15:0] dataIn,
  input  clk,
  input  writeEnable,
  input  reset,
  output [15:0] dataOut
);

  wire clk_t;

  and and_1 (clk_t, clk, writeEnable);
  D_Flip_Flop d_ff_1 (.D(dataIn[0]), .clk(clk_t), .Q(dataOut[0]), .reset(reset));  // open: Qn, preset
  D_Flip_Flop d_ff_2 (.D(dataIn[1]), .clk(clk_t), .Q(dataOut[1]), .reset(reset));  // open: Qn, preset
  D_Flip_Flop d_ff_3 (.D(dataIn[2]), .clk(clk_t), .Q(dataOut[2]), .reset(reset));  // open: Qn, preset
  D_Flip_Flop d_ff_4 (.D(dataIn[3]), .clk(clk_t), .Q(dataOut[3]), .reset(reset));  // open: Qn, preset
  D_Flip_Flop d_ff_5 (.D(dataIn[4]), .clk(clk_t), .Q(dataOut[4]), .reset(reset));  // open: Qn, preset
  D_Flip_Flop d_ff_6 (.D(dataIn[5]), .clk(clk_t), .Q(dataOut[5]), .reset(reset));  // open: Qn, preset
  D_Flip_Flop d_ff_7 (.D(dataIn[6]), .clk(clk_t), .Q(dataOut[6]), .reset(reset));  // open: Qn, preset
  D_Flip_Flop d_ff_8 (.D(dataIn[7]), .clk(clk_t), .Q(dataOut[7]), .reset(reset));  // open: Qn, preset
  D_Flip_Flop d_ff_9 (.D(dataIn[8]), .clk(clk_t), .Q(dataOut[8]), .reset(reset));  // open: Qn, preset
  D_Flip_Flop d_ff_10 (.D(dataIn[9]), .clk(clk_t), .Q(dataOut[9]), .reset(reset));  // open: Qn, preset
  D_Flip_Flop d_ff_11 (.D(dataIn[10]), .clk(clk_t), .Q(dataOut[10]), .reset(reset));  // open: Qn, preset
  D_Flip_Flop d_ff_12 (.D(dataIn[11]), .clk(clk_t), .Q(dataOut[11]), .reset(reset));  // open: Qn, preset
  D_Flip_Flop d_ff_13 (.D(dataIn[12]), .clk(clk_t), .Q(dataOut[12]), .reset(reset));  // open: Qn, preset
  D_Flip_Flop d_ff_14 (.D(dataIn[13]), .clk(clk_t), .Q(dataOut[13]), .reset(reset));  // open: Qn, preset
  D_Flip_Flop d_ff_15 (.D(dataIn[14]), .clk(clk_t), .Q(dataOut[14]), .reset(reset));  // open: Qn, preset
  D_Flip_Flop d_ff_16 (.D(dataIn[15]), .clk(clk_t), .Q(dataOut[15]), .reset(reset));  // open: Qn, preset

  // Other names for the same wires on the sheet: in0 = dataIn[0]; in1 = dataIn[1]; in2 = dataIn[2]; in3 = dataIn[3];
  //   in4 = dataIn[4]; in5 = dataIn[5]; in6 = dataIn[6]; in7 = dataIn[7]; in8 = dataIn[8]; in9 = dataIn[9];
  //   in10 = dataIn[10]; in11 = dataIn[11]; in12 = dataIn[12]; in13 = dataIn[13]; in14 = dataIn[14];
  //   in15 = dataIn[15]; out0 = dataOut[0]; out1 = dataOut[1]; out2 = dataOut[2]; out3 = dataOut[3];
  //   out4 = dataOut[4]; out5 = dataOut[5]; out6 = dataOut[6]; out7 = dataOut[7]; out8 = dataOut[8];
  //   out9 = dataOut[9]; out10 = dataOut[10]; out11 = dataOut[11]; out12 = dataOut[12]; out13 = dataOut[13];
  //   out14 = dataOut[14]; out15 = dataOut[15]
endmodule

module RegisterFile (
  input  clk,
  input  [15:0] WriteData,
  input  reset,
  input  RegWriteEnable,
  input  [2:0] WritePort,
  input  [2:0] ReadReg2,
  input  [2:0] ReadReg1,
  output [15:0] Reg1Contents,
  output [15:0] Reg2Contents
);

  wire rd0, rd1, rd2, rd3, rd4, rd5, rd6, rd7, rs0, rs1, rs2, rs3, rs4, rs5, rs6, rs7, rt0, rt1, rt2, rt3,
       rt4, rt5, rt6, rt7;
  wire [15:0] register0_dataout, register1_dataout, register2_dataout, register3_dataout, register4_dataout,
       register5_dataout, register6_dataout, register7_dataout;

  Decoder #(.select(3)) decoder_1 (
    .out0(rs0), .out1(rs1), .out2(rs2), .out3(rs3), .out4(rs4), .out5(rs5), .out6(rs6), .out7(rs7),
    .sel(ReadReg1));  // open: en
  // Probe on register0_dataout
  // Probe on register1_dataout
  // Probe on register2_dataout
  // Probe on register3_dataout
  // Probe on register4_dataout
  // Probe on register5_dataout
  // Probe on register6_dataout
  // Probe on register7_dataout
  Decoder #(.select(3)) decoder_2 (
    .out0(rt0), .out1(rt1), .out2(rt2), .out3(rt3), .out4(rt4), .out5(rt5), .out6(rt6), .out7(rt7),
    .sel(ReadReg2));  // open: en
  SingleRegister register0 (
    .dataIn({16{1'b0}}), .clk(clk), .writeEnable(rd0), .reset(reset), .dataOut(register0_dataout));
  SingleRegister register1 (
    .dataIn(WriteData), .clk(clk), .writeEnable(rd1), .reset(reset), .dataOut(register1_dataout));
  SingleRegister register2 (
    .dataIn(WriteData), .clk(clk), .writeEnable(rd2), .reset(reset), .dataOut(register2_dataout));
  SingleRegister register3 (
    .dataIn(WriteData), .clk(clk), .writeEnable(rd3), .reset(reset), .dataOut(register3_dataout));
  SingleRegister register4 (
    .dataIn(WriteData), .clk(clk), .writeEnable(rd4), .reset(reset), .dataOut(register4_dataout));
  SingleRegister register5 (
    .dataIn(WriteData), .clk(clk), .writeEnable(rd5), .reset(reset), .dataOut(register5_dataout));
  SingleRegister register6 (
    .dataIn(WriteData), .clk(clk), .writeEnable(rd6), .reset(reset), .dataOut(register6_dataout));
  SingleRegister register7 (
    .dataIn(WriteData), .clk(clk), .writeEnable(rd7), .reset(reset), .dataOut(register7_dataout));
  assign Reg1Contents = rs0 ? register0_dataout : 16'bz;  // Controlled_Buffer controlled_buffer_1
  assign Reg2Contents = rt0 ? register0_dataout : 16'bz;  // Controlled_Buffer controlled_buffer_2
  assign Reg1Contents = rs1 ? register1_dataout : 16'bz;  // Controlled_Buffer controlled_buffer_3
  assign Reg2Contents = rt1 ? register1_dataout : 16'bz;  // Controlled_Buffer controlled_buffer_4
  assign Reg1Contents = rs2 ? register2_dataout : 16'bz;  // Controlled_Buffer controlled_buffer_5
  assign Reg2Contents = rt2 ? register2_dataout : 16'bz;  // Controlled_Buffer controlled_buffer_6
  assign Reg1Contents = rs3 ? register3_dataout : 16'bz;  // Controlled_Buffer controlled_buffer_7
  assign Reg2Contents = rt3 ? register3_dataout : 16'bz;  // Controlled_Buffer controlled_buffer_8
  assign Reg1Contents = rs4 ? register4_dataout : 16'bz;  // Controlled_Buffer controlled_buffer_9
  assign Reg2Contents = rt4 ? register4_dataout : 16'bz;  // Controlled_Buffer controlled_buffer_10
  assign Reg1Contents = rs5 ? register5_dataout : 16'bz;  // Controlled_Buffer controlled_buffer_11
  assign Reg2Contents = rt5 ? register5_dataout : 16'bz;  // Controlled_Buffer controlled_buffer_12
  assign Reg1Contents = rs6 ? register6_dataout : 16'bz;  // Controlled_Buffer controlled_buffer_13
  assign Reg2Contents = rt6 ? register6_dataout : 16'bz;  // Controlled_Buffer controlled_buffer_14
  assign Reg1Contents = rs7 ? register7_dataout : 16'bz;  // Controlled_Buffer controlled_buffer_15
  assign Reg2Contents = rt7 ? register7_dataout : 16'bz;  // Controlled_Buffer controlled_buffer_16
  Decoder #(.select(3)) decoder_3 (
    .out0(rd0), .out1(rd1), .out2(rd2), .out3(rd3), .out4(rd4), .out5(rd5), .out6(rd6), .out7(rd7),
    .sel(WritePort), .en(RegWriteEnable));
endmodule

module ALU (
  input  [15:0] InputData1,
  input  [15:0] InputData2,
  input  [2:0] OpType,
  input  [2:0] ShiftAmount,
  output [15:0] OutputData
);

  wire [15:0] Addition_result, leftshift_1_outputdata, not_result, rightshift_1_outputdata,
       Subtraction_result, xor_result;

  assign not_result = ~InputData1;  // NOT_Gate not_1, 16 bits wide
  // Probe on not_result
  assign xor_result = InputData2 ^ InputData1;  // XOR_Gate xor_1, 16 bits wide
  LeftShift leftshift_1 (.ShiftAmount(ShiftAmount), .InputData(InputData1), .OutputData(leftshift_1_outputdata));
  RightShift rightshift_1 (.ShiftAmount(ShiftAmount), .InputData(InputData1), .OutputData(rightshift_1_outputdata));
  Adding Subtraction (.sub(1'b1), .B(InputData2), .A(InputData1), .result(Subtraction_result));  // open: ovf
  Adding Addition (.sub(1'b0), .B(InputData2), .A(InputData1), .result(Addition_result));  // open: ovf
  Multiplexer #(.select(3), .width(16), .enable("false")) multiplexer_1 (
    .in0(Addition_result), .in1(Subtraction_result), .in2(Addition_result), .in3(not_result),
    .in4(xor_result), .in5(leftshift_1_outputdata), .in6(rightshift_1_outputdata), .out(OutputData),
    .sel(OpType));  // open: in7
endmodule

module FullAdder (
  input  Cin,
  input  A,
  input  B,
  output Sum,
  output Cout
);

  wire and_1_out, and_2_out, xor_1_out;

  and and_1 (and_1_out, B, A);
  xor xor_1 (xor_1_out, A, B);
  or or_1 (Cout, and_1_out, and_2_out);
  and and_2 (and_2_out, xor_1_out, Cin);
  xor xor_2 (Sum, Cin, xor_1_out);
endmodule

module Adding (
  input  sub,
  input  [15:0] B,
  input  [15:0] A,
  output [15:0] result,
  output ovf
);

  wire CO0, CO1, CO2, CO3, CO4, CO5, CO6, CO7, CO8, CO9, CO10, CO11, CO12, CO13, CO14, fulladder_1_cout,
       xor_2_out, xor_3_out, xor_4_out, xor_5_out, xor_6_out, xor_7_out, xor_8_out, xor_9_out, xor_10_out,
       xor_11_out, xor_12_out, xor_13_out, xor_14_out, xor_15_out, xor_16_out, xor_17_out;

  xor xor_1 (ovf, CO14, fulladder_1_cout);
  FullAdder fulladder_1 (.Cin(CO14), .A(xor_2_out), .B(A[15]), .Sum(result[15]), .Cout(fulladder_1_cout));
  xor xor_2 (xor_2_out, sub, B[15]);
  FullAdder fulladder_2 (.Cin(CO13), .A(xor_3_out), .B(A[14]), .Sum(result[14]), .Cout(CO14));
  xor xor_3 (xor_3_out, sub, B[14]);
  FullAdder fulladder_3 (.Cin(CO12), .A(xor_4_out), .B(A[13]), .Sum(result[13]), .Cout(CO13));
  xor xor_4 (xor_4_out, sub, B[13]);
  FullAdder fulladder_4 (.Cin(CO11), .A(xor_5_out), .B(A[12]), .Sum(result[12]), .Cout(CO12));
  xor xor_5 (xor_5_out, sub, B[12]);
  FullAdder fulladder_5 (.Cin(CO10), .A(xor_6_out), .B(A[11]), .Sum(result[11]), .Cout(CO11));
  xor xor_6 (xor_6_out, sub, B[11]);
  FullAdder fulladder_6 (.Cin(CO9), .A(xor_7_out), .B(A[10]), .Sum(result[10]), .Cout(CO10));
  xor xor_7 (xor_7_out, sub, B[10]);
  FullAdder fulladder_7 (.Cin(CO8), .A(xor_8_out), .B(A[9]), .Sum(result[9]), .Cout(CO9));
  xor xor_8 (xor_8_out, sub, B[9]);
  FullAdder fulladder_8 (.Cin(CO7), .A(xor_9_out), .B(A[8]), .Sum(result[8]), .Cout(CO8));
  xor xor_9 (xor_9_out, sub, B[8]);
  FullAdder fulladder_9 (.Cin(CO6), .A(xor_10_out), .B(A[7]), .Sum(result[7]), .Cout(CO7));
  xor xor_10 (xor_10_out, sub, B[7]);
  FullAdder fulladder_10 (.Cin(CO5), .A(xor_11_out), .B(A[6]), .Sum(result[6]), .Cout(CO6));
  xor xor_11 (xor_11_out, sub, B[6]);
  FullAdder fulladder_11 (.Cin(CO4), .A(xor_12_out), .B(A[5]), .Sum(result[5]), .Cout(CO5));
  xor xor_12 (xor_12_out, sub, B[5]);
  FullAdder fulladder_12 (.Cin(CO3), .A(xor_13_out), .B(A[4]), .Sum(result[4]), .Cout(CO4));
  xor xor_13 (xor_13_out, sub, B[4]);
  FullAdder fulladder_13 (.Cin(CO2), .A(xor_14_out), .B(A[3]), .Sum(result[3]), .Cout(CO3));
  xor xor_14 (xor_14_out, sub, B[3]);
  FullAdder fulladder_14 (.Cin(CO1), .A(xor_15_out), .B(A[2]), .Sum(result[2]), .Cout(CO2));
  xor xor_15 (xor_15_out, sub, B[2]);
  FullAdder fulladder_15 (.Cin(CO0), .A(xor_16_out), .B(A[1]), .Sum(result[1]), .Cout(CO1));
  xor xor_16 (xor_16_out, sub, B[1]);
  FullAdder fulladder_16 (.Cin(sub), .A(xor_17_out), .B(A[0]), .Sum(result[0]), .Cout(CO0));
  xor xor_17 (xor_17_out, sub, B[0]);

  // Other names for the same wires on the sheet: S0 = result[0]; S1 = result[1]; S2 = result[2]; S3 = result[3];
  //   S4 = result[4]; S5 = result[5]; S6 = result[6]; S7 = result[7]; S8 = result[8]; S9 = result[9];
  //   S10 = result[10]; S11 = result[11]; S12 = result[12]; S13 = result[13]; S14 = result[14]; S15 = result[15]
endmodule

module LeftShift (
  input  [2:0] ShiftAmount,
  input  [15:0] InputData,
  output [15:0] OutputData
);

  wire multiplexer_1_out, multiplexer_2_out, multiplexer_3_out, multiplexer_4_out, multiplexer_5_out,
       multiplexer_6_out, multiplexer_7_out, multiplexer_8_out, multiplexer_9_out, multiplexer_10_out,
       multiplexer_11_out, multiplexer_12_out, multiplexer_13_out, multiplexer_14_out, multiplexer_15_out,
       multiplexer_16_out, multiplexer_17_out, multiplexer_18_out, multiplexer_19_out, multiplexer_20_out,
       multiplexer_21_out, multiplexer_22_out, multiplexer_23_out, multiplexer_24_out, multiplexer_25_out,
       multiplexer_26_out, multiplexer_27_out, multiplexer_28_out, multiplexer_29_out, multiplexer_30_out,
       multiplexer_31_out, multiplexer_32_out;

  Multiplexer #(.enable("false")) multiplexer_1 (
    .in0(InputData[15]), .in1(InputData[14]), .out(multiplexer_1_out), .sel(ShiftAmount[0]));
  Multiplexer #(.enable("false")) multiplexer_2 (
    .in0(InputData[14]), .in1(InputData[13]), .out(multiplexer_2_out), .sel(ShiftAmount[0]));
  Multiplexer #(.enable("false")) multiplexer_3 (
    .in0(InputData[13]), .in1(InputData[12]), .out(multiplexer_3_out), .sel(ShiftAmount[0]));
  Multiplexer #(.enable("false")) multiplexer_4 (
    .in0(InputData[12]), .in1(InputData[11]), .out(multiplexer_4_out), .sel(ShiftAmount[0]));
  Multiplexer #(.enable("false")) multiplexer_5 (
    .in0(InputData[11]), .in1(InputData[10]), .out(multiplexer_5_out), .sel(ShiftAmount[0]));
  Multiplexer #(.enable("false")) multiplexer_6 (
    .in0(InputData[10]), .in1(InputData[9]), .out(multiplexer_6_out), .sel(ShiftAmount[0]));
  Multiplexer #(.enable("false")) multiplexer_7 (
    .in0(InputData[9]), .in1(InputData[8]), .out(multiplexer_7_out), .sel(ShiftAmount[0]));
  Multiplexer #(.enable("false")) multiplexer_8 (
    .in0(InputData[8]), .in1(InputData[7]), .out(multiplexer_8_out), .sel(ShiftAmount[0]));
  Multiplexer #(.enable("false")) multiplexer_9 (
    .in0(InputData[7]), .in1(InputData[6]), .out(multiplexer_9_out), .sel(ShiftAmount[0]));
  Multiplexer #(.enable("false")) multiplexer_10 (
    .in0(InputData[6]), .in1(InputData[5]), .out(multiplexer_10_out), .sel(ShiftAmount[0]));
  Multiplexer #(.enable("false")) multiplexer_11 (
    .in0(InputData[5]), .in1(InputData[4]), .out(multiplexer_11_out), .sel(ShiftAmount[0]));
  Multiplexer #(.enable("false")) multiplexer_12 (
    .in0(InputData[4]), .in1(InputData[3]), .out(multiplexer_12_out), .sel(ShiftAmount[0]));
  Multiplexer #(.enable("false")) multiplexer_13 (
    .in0(InputData[3]), .in1(InputData[2]), .out(multiplexer_13_out), .sel(ShiftAmount[0]));
  Multiplexer #(.enable("false")) multiplexer_14 (
    .in0(InputData[2]), .in1(InputData[1]), .out(multiplexer_14_out), .sel(ShiftAmount[0]));
  Multiplexer #(.enable("false")) multiplexer_15 (
    .in0(InputData[1]), .in1(InputData[0]), .out(multiplexer_15_out), .sel(ShiftAmount[0]));
  Multiplexer #(.enable("false")) multiplexer_16 (
    .in0(InputData[0]), .in1(1'b0), .out(multiplexer_16_out), .sel(ShiftAmount[0]));
  Multiplexer #(.enable("false")) multiplexer_17 (
    .in0(multiplexer_1_out), .in1(multiplexer_3_out), .out(multiplexer_17_out), .sel(ShiftAmount[1]));
  Multiplexer #(.enable("false")) multiplexer_18 (
    .in0(multiplexer_2_out), .in1(multiplexer_4_out), .out(multiplexer_18_out), .sel(ShiftAmount[1]));
  Multiplexer #(.enable("false")) multiplexer_19 (
    .in0(multiplexer_3_out), .in1(multiplexer_5_out), .out(multiplexer_19_out), .sel(ShiftAmount[1]));
  Multiplexer #(.enable("false")) multiplexer_20 (
    .in0(multiplexer_4_out), .in1(multiplexer_6_out), .out(multiplexer_20_out), .sel(ShiftAmount[1]));
  Multiplexer #(.enable("false")) multiplexer_21 (
    .in0(multiplexer_5_out), .in1(multiplexer_7_out), .out(multiplexer_21_out), .sel(ShiftAmount[1]));
  Multiplexer #(.enable("false")) multiplexer_22 (
    .in0(multiplexer_6_out), .in1(multiplexer_8_out), .out(multiplexer_22_out), .sel(ShiftAmount[1]));
  Multiplexer #(.enable("false")) multiplexer_23 (
    .in0(multiplexer_7_out), .in1(multiplexer_9_out), .out(multiplexer_23_out), .sel(ShiftAmount[1]));
  Multiplexer #(.enable("false")) multiplexer_24 (
    .in0(multiplexer_8_out), .in1(multiplexer_10_out), .out(multiplexer_24_out), .sel(ShiftAmount[1]));
  Multiplexer #(.enable("false")) multiplexer_25 (
    .in0(multiplexer_9_out), .in1(multiplexer_11_out), .out(multiplexer_25_out), .sel(ShiftAmount[1]));
  Multiplexer #(.enable("false")) multiplexer_26 (
    .in0(multiplexer_10_out), .in1(multiplexer_12_out), .out(multiplexer_26_out), .sel(ShiftAmount[1]));
  Multiplexer #(.enable("false")) multiplexer_27 (
    .in0(multiplexer_11_out), .in1(multiplexer_13_out), .out(multiplexer_27_out), .sel(ShiftAmount[1]));
  Multiplexer #(.enable("false")) multiplexer_28 (
    .in0(multiplexer_12_out), .in1(multiplexer_14_out), .out(multiplexer_28_out), .sel(ShiftAmount[1]));
  Multiplexer #(.enable("false")) multiplexer_29 (
    .in0(multiplexer_13_out), .in1(multiplexer_15_out), .out(multiplexer_29_out), .sel(ShiftAmount[1]));
  Multiplexer #(.enable("false")) multiplexer_30 (
    .in0(multiplexer_14_out), .in1(multiplexer_16_out), .out(multiplexer_30_out), .sel(ShiftAmount[1]));
  Multiplexer #(.enable("false")) multiplexer_31 (
    .in0(multiplexer_15_out), .in1(1'b0), .out(multiplexer_31_out), .sel(ShiftAmount[1]));
  Multiplexer #(.enable("false")) multiplexer_32 (
    .in0(multiplexer_16_out), .in1(1'b0), .out(multiplexer_32_out), .sel(ShiftAmount[1]));
  Multiplexer #(.enable("false")) multiplexer_33 (
    .in0(multiplexer_17_out), .in1(multiplexer_21_out), .out(OutputData[15]), .sel(ShiftAmount[2]));
  Multiplexer #(.enable("false")) multiplexer_34 (
    .in0(multiplexer_18_out), .in1(multiplexer_22_out), .out(OutputData[14]), .sel(ShiftAmount[2]));
  Multiplexer #(.enable("false")) multiplexer_35 (
    .in0(multiplexer_19_out), .in1(multiplexer_23_out), .out(OutputData[13]), .sel(ShiftAmount[2]));
  Multiplexer #(.enable("false")) multiplexer_36 (
    .in0(multiplexer_20_out), .in1(multiplexer_24_out), .out(OutputData[12]), .sel(ShiftAmount[2]));
  Multiplexer #(.enable("false")) multiplexer_37 (
    .in0(multiplexer_21_out), .in1(multiplexer_25_out), .out(OutputData[11]), .sel(ShiftAmount[2]));
  Multiplexer #(.enable("false")) multiplexer_38 (
    .in0(multiplexer_22_out), .in1(multiplexer_26_out), .out(OutputData[10]), .sel(ShiftAmount[2]));
  Multiplexer #(.enable("false")) multiplexer_39 (
    .in0(multiplexer_23_out), .in1(multiplexer_27_out), .out(OutputData[9]), .sel(ShiftAmount[2]));
  Multiplexer #(.enable("false")) multiplexer_40 (
    .in0(multiplexer_24_out), .in1(multiplexer_28_out), .out(OutputData[8]), .sel(ShiftAmount[2]));
  Multiplexer #(.enable("false")) multiplexer_41 (
    .in0(multiplexer_25_out), .in1(multiplexer_29_out), .out(OutputData[7]), .sel(ShiftAmount[2]));
  Multiplexer #(.enable("false")) multiplexer_42 (
    .in0(multiplexer_26_out), .in1(multiplexer_30_out), .out(OutputData[6]), .sel(ShiftAmount[2]));
  Multiplexer #(.enable("false")) multiplexer_43 (
    .in0(multiplexer_27_out), .in1(multiplexer_31_out), .out(OutputData[5]), .sel(ShiftAmount[2]));
  Multiplexer #(.enable("false")) multiplexer_44 (
    .in0(multiplexer_28_out), .in1(multiplexer_32_out), .out(OutputData[4]), .sel(ShiftAmount[2]));
  Multiplexer #(.enable("false")) multiplexer_45 (
    .in0(multiplexer_29_out), .in1(1'b0), .out(OutputData[3]), .sel(ShiftAmount[2]));
  Multiplexer #(.enable("false")) multiplexer_46 (
    .in0(multiplexer_30_out), .in1(1'b0), .out(OutputData[2]), .sel(ShiftAmount[2]));
  Multiplexer #(.enable("false")) multiplexer_47 (
    .in0(multiplexer_31_out), .in1(1'b0), .out(OutputData[1]), .sel(ShiftAmount[2]));
  Multiplexer #(.enable("false")) multiplexer_48 (
    .in0(multiplexer_32_out), .in1(1'b0), .out(OutputData[0]), .sel(ShiftAmount[2]));

  // Other names for the same wires on the sheet: input0 = InputData[0]; input1 = InputData[1]; input2 = InputData[2];
  //   input3 = InputData[3]; input4 = InputData[4]; input5 = InputData[5]; input6 = InputData[6];
  //   input7 = InputData[7]; input8 = InputData[8]; input9 = InputData[9]; input10 = InputData[10];
  //   input11 = InputData[11]; input12 = InputData[12]; input13 = InputData[13]; input14 = InputData[14];
  //   input15 = InputData[15]; output0 = OutputData[0]; output1 = OutputData[1]; output2 = OutputData[2];
  //   output3 = OutputData[3]; output4 = OutputData[4]; output5 = OutputData[5]; output6 = OutputData[6];
  //   output7 = OutputData[7]; output8 = OutputData[8]; output9 = OutputData[9]; output10 = OutputData[10];
  //   output11 = OutputData[11]; output12 = OutputData[12]; output13 = OutputData[13]; output14 = OutputData[14];
  //   output15 = OutputData[15]; shift0 = ShiftAmount[0]; shift1 = ShiftAmount[1]; shift2 = ShiftAmount[2]
endmodule

module RightShift (
  input  [2:0] ShiftAmount,
  input  [15:0] InputData,
  output [15:0] OutputData
);

  wire multiplexer_1_out, multiplexer_2_out, multiplexer_3_out, multiplexer_4_out, multiplexer_5_out,
       multiplexer_6_out, multiplexer_7_out, multiplexer_8_out, multiplexer_9_out, multiplexer_10_out,
       multiplexer_11_out, multiplexer_12_out, multiplexer_13_out, multiplexer_14_out, multiplexer_15_out,
       multiplexer_16_out, multiplexer_17_out, multiplexer_18_out, multiplexer_19_out, multiplexer_20_out,
       multiplexer_21_out, multiplexer_22_out, multiplexer_23_out, multiplexer_24_out, multiplexer_25_out,
       multiplexer_26_out, multiplexer_27_out, multiplexer_28_out, multiplexer_29_out, multiplexer_30_out,
       multiplexer_31_out, multiplexer_32_out;

  Multiplexer #(.enable("false")) multiplexer_1 (
    .in0(InputData[0]), .in1(InputData[1]), .out(multiplexer_1_out), .sel(ShiftAmount[0]));
  Multiplexer #(.enable("false")) multiplexer_2 (
    .in0(InputData[1]), .in1(InputData[2]), .out(multiplexer_2_out), .sel(ShiftAmount[0]));
  Multiplexer #(.enable("false")) multiplexer_3 (
    .in0(InputData[2]), .in1(InputData[3]), .out(multiplexer_3_out), .sel(ShiftAmount[0]));
  Multiplexer #(.enable("false")) multiplexer_4 (
    .in0(InputData[3]), .in1(InputData[4]), .out(multiplexer_4_out), .sel(ShiftAmount[0]));
  Multiplexer #(.enable("false")) multiplexer_5 (
    .in0(InputData[4]), .in1(InputData[5]), .out(multiplexer_5_out), .sel(ShiftAmount[0]));
  Multiplexer #(.enable("false")) multiplexer_6 (
    .in0(InputData[5]), .in1(InputData[6]), .out(multiplexer_6_out), .sel(ShiftAmount[0]));
  Multiplexer #(.enable("false")) multiplexer_7 (
    .in0(InputData[6]), .in1(InputData[7]), .out(multiplexer_7_out), .sel(ShiftAmount[0]));
  Multiplexer #(.enable("false")) multiplexer_8 (
    .in0(InputData[7]), .in1(InputData[8]), .out(multiplexer_8_out), .sel(ShiftAmount[0]));
  Multiplexer #(.enable("false")) multiplexer_9 (
    .in0(InputData[8]), .in1(InputData[9]), .out(multiplexer_9_out), .sel(ShiftAmount[0]));
  Multiplexer #(.enable("false")) multiplexer_10 (
    .in0(InputData[9]), .in1(InputData[10]), .out(multiplexer_10_out), .sel(ShiftAmount[0]));
  Multiplexer #(.enable("false")) multiplexer_11 (
    .in0(InputData[10]), .in1(InputData[11]), .out(multiplexer_11_out), .sel(ShiftAmount[0]));
  Multiplexer #(.enable("false")) multiplexer_12 (
    .in0(InputData[11]), .in1(InputData[12]), .out(multiplexer_12_out), .sel(ShiftAmount[0]));
  Multiplexer #(.enable("false")) multiplexer_13 (
    .in0(InputData[12]), .in1(InputData[13]), .out(multiplexer_13_out), .sel(ShiftAmount[0]));
  Multiplexer #(.enable("false")) multiplexer_14 (
    .in0(InputData[13]), .in1(InputData[14]), .out(multiplexer_14_out), .sel(ShiftAmount[0]));
  Multiplexer #(.enable("false")) multiplexer_15 (
    .in0(InputData[14]), .in1(InputData[15]), .out(multiplexer_15_out), .sel(ShiftAmount[0]));
  Multiplexer #(.enable("false")) multiplexer_16 (
    .in0(InputData[15]), .in1(1'b0), .out(multiplexer_16_out), .sel(ShiftAmount[0]));
  Multiplexer #(.enable("false")) multiplexer_17 (
    .in0(multiplexer_1_out), .in1(multiplexer_3_out), .out(multiplexer_17_out), .sel(ShiftAmount[1]));
  Multiplexer #(.enable("false")) multiplexer_18 (
    .in0(multiplexer_2_out), .in1(multiplexer_4_out), .out(multiplexer_18_out), .sel(ShiftAmount[1]));
  Multiplexer #(.enable("false")) multiplexer_19 (
    .in0(multiplexer_3_out), .in1(multiplexer_5_out), .out(multiplexer_19_out), .sel(ShiftAmount[1]));
  Multiplexer #(.enable("false")) multiplexer_20 (
    .in0(multiplexer_4_out), .in1(multiplexer_6_out), .out(multiplexer_20_out), .sel(ShiftAmount[1]));
  Multiplexer #(.enable("false")) multiplexer_21 (
    .in0(multiplexer_5_out), .in1(multiplexer_7_out), .out(multiplexer_21_out), .sel(ShiftAmount[1]));
  Multiplexer #(.enable("false")) multiplexer_22 (
    .in0(multiplexer_6_out), .in1(multiplexer_8_out), .out(multiplexer_22_out), .sel(ShiftAmount[1]));
  Multiplexer #(.enable("false")) multiplexer_23 (
    .in0(multiplexer_7_out), .in1(multiplexer_9_out), .out(multiplexer_23_out), .sel(ShiftAmount[1]));
  Multiplexer #(.enable("false")) multiplexer_24 (
    .in0(multiplexer_8_out), .in1(multiplexer_10_out), .out(multiplexer_24_out), .sel(ShiftAmount[1]));
  Multiplexer #(.enable("false")) multiplexer_25 (
    .in0(multiplexer_9_out), .in1(multiplexer_11_out), .out(multiplexer_25_out), .sel(ShiftAmount[1]));
  Multiplexer #(.enable("false")) multiplexer_26 (
    .in0(multiplexer_10_out), .in1(multiplexer_12_out), .out(multiplexer_26_out), .sel(ShiftAmount[1]));
  Multiplexer #(.enable("false")) multiplexer_27 (
    .in0(multiplexer_11_out), .in1(multiplexer_13_out), .out(multiplexer_27_out), .sel(ShiftAmount[1]));
  Multiplexer #(.enable("false")) multiplexer_28 (
    .in0(multiplexer_12_out), .in1(multiplexer_14_out), .out(multiplexer_28_out), .sel(ShiftAmount[1]));
  Multiplexer #(.enable("false")) multiplexer_29 (
    .in0(multiplexer_13_out), .in1(multiplexer_15_out), .out(multiplexer_29_out), .sel(ShiftAmount[1]));
  Multiplexer #(.enable("false")) multiplexer_30 (
    .in0(multiplexer_14_out), .in1(multiplexer_16_out), .out(multiplexer_30_out), .sel(ShiftAmount[1]));
  Multiplexer #(.enable("false")) multiplexer_31 (
    .in0(multiplexer_15_out), .in1(1'b0), .out(multiplexer_31_out), .sel(ShiftAmount[1]));
  Multiplexer #(.enable("false")) multiplexer_32 (
    .in0(multiplexer_16_out), .in1(1'b0), .out(multiplexer_32_out), .sel(ShiftAmount[1]));
  Multiplexer #(.enable("false")) multiplexer_33 (
    .in0(multiplexer_17_out), .in1(multiplexer_21_out), .out(OutputData[0]), .sel(ShiftAmount[2]));
  Multiplexer #(.enable("false")) multiplexer_34 (
    .in0(multiplexer_18_out), .in1(multiplexer_22_out), .out(OutputData[1]), .sel(ShiftAmount[2]));
  Multiplexer #(.enable("false")) multiplexer_35 (
    .in0(multiplexer_19_out), .in1(multiplexer_23_out), .out(OutputData[2]), .sel(ShiftAmount[2]));
  Multiplexer #(.enable("false")) multiplexer_36 (
    .in0(multiplexer_20_out), .in1(multiplexer_24_out), .out(OutputData[3]), .sel(ShiftAmount[2]));
  Multiplexer #(.enable("false")) multiplexer_37 (
    .in0(multiplexer_21_out), .in1(multiplexer_25_out), .out(OutputData[4]), .sel(ShiftAmount[2]));
  Multiplexer #(.enable("false")) multiplexer_38 (
    .in0(multiplexer_22_out), .in1(multiplexer_26_out), .out(OutputData[5]), .sel(ShiftAmount[2]));
  Multiplexer #(.enable("false")) multiplexer_39 (
    .in0(multiplexer_23_out), .in1(multiplexer_27_out), .out(OutputData[6]), .sel(ShiftAmount[2]));
  Multiplexer #(.enable("false")) multiplexer_40 (
    .in0(multiplexer_24_out), .in1(multiplexer_28_out), .out(OutputData[7]), .sel(ShiftAmount[2]));
  Multiplexer #(.enable("false")) multiplexer_41 (
    .in0(multiplexer_25_out), .in1(multiplexer_29_out), .out(OutputData[8]), .sel(ShiftAmount[2]));
  Multiplexer #(.enable("false")) multiplexer_42 (
    .in0(multiplexer_26_out), .in1(multiplexer_30_out), .out(OutputData[9]), .sel(ShiftAmount[2]));
  Multiplexer #(.enable("false")) multiplexer_43 (
    .in0(multiplexer_27_out), .in1(multiplexer_31_out), .out(OutputData[10]), .sel(ShiftAmount[2]));
  Multiplexer #(.enable("false")) multiplexer_44 (
    .in0(multiplexer_28_out), .in1(multiplexer_32_out), .out(OutputData[11]), .sel(ShiftAmount[2]));
  Multiplexer #(.enable("false")) multiplexer_45 (
    .in0(multiplexer_29_out), .in1(1'b0), .out(OutputData[12]), .sel(ShiftAmount[2]));
  Multiplexer #(.enable("false")) multiplexer_46 (
    .in0(multiplexer_30_out), .in1(1'b0), .out(OutputData[13]), .sel(ShiftAmount[2]));
  Multiplexer #(.enable("false")) multiplexer_47 (
    .in0(multiplexer_31_out), .in1(1'b0), .out(OutputData[14]), .sel(ShiftAmount[2]));
  Multiplexer #(.enable("false")) multiplexer_48 (
    .in0(multiplexer_32_out), .in1(1'b0), .out(OutputData[15]), .sel(ShiftAmount[2]));

  // Other names for the same wires on the sheet: input0 = InputData[0]; input1 = InputData[1]; input2 = InputData[2];
  //   input3 = InputData[3]; input4 = InputData[4]; input5 = InputData[5]; input6 = InputData[6];
  //   input7 = InputData[7]; input8 = InputData[8]; input9 = InputData[9]; input10 = InputData[10];
  //   input11 = InputData[11]; input12 = InputData[12]; input13 = InputData[13]; input14 = InputData[14];
  //   input15 = InputData[15]; output0 = OutputData[0]; output1 = OutputData[1]; output2 = OutputData[2];
  //   output3 = OutputData[3]; output4 = OutputData[4]; output5 = OutputData[5]; output6 = OutputData[6];
  //   output7 = OutputData[7]; output8 = OutputData[8]; output9 = OutputData[9]; output10 = OutputData[10];
  //   output11 = OutputData[11]; output12 = OutputData[12]; output13 = OutputData[13]; output14 = OutputData[14];
  //   output15 = OutputData[15]; shift0 = ShiftAmount[0]; shift1 = ShiftAmount[1]; shift2 = ShiftAmount[2]
endmodule

module InstructionDecoder (
  input  [3:0] opcode,
  output RWE,
  output destination,
  output [2:0] ALUinput,
  output ShiftAmount,
  output writeImmediate,
  output NotOrShifting,
  output invert,
  output StoreWord,
  output LoadWord,
  output LoadWordStoreWord,
  output blt,
  output beqz,
  output inputaur,
  output outputaur,
  output JalOrJ,
  output jal,
  output jr
);

  wire add, addi, j, sllaur, srlaur, sub, xoraur;

  Decoder #(.select(4)) decoder_1 (
    .out0(add), .out1(sub), .out2(addi), .out3(invert), .out4(xoraur), .out5(sllaur), .out6(srlaur),
    .out7(LoadWord), .out8(StoreWord), .out9(beqz), .out10(blt), .out11(j), .out12(jr), .out13(jal),
    .out14(inputaur), .out15(outputaur), .sel(opcode));  // open: en
  or or_1 (ALUinput[0], sub, invert, sllaur);
  or or_2 (ALUinput[1], addi, invert, srlaur);
  or or_3 (ALUinput[2], xoraur, sllaur, srlaur);
  or or_4 (RWE, addi, LoadWord);
  or or_5 (writeImmediate, addi, StoreWord, LoadWord);
  or or_6 (JalOrJ, j, jal);
  or or_7 (destination, beqz, blt, j, jr, outputaur, StoreWord);
  or or_8 (ShiftAmount, sllaur, srlaur);
  or or_9 (NotOrShifting, invert, srlaur, sllaur);
  or or_10 (LoadWordStoreWord, StoreWord, LoadWord);

  // Other names for the same wires on the sheet: lw = LoadWord; naur = invert; sw = StoreWord
endmodule

module ReadROM (
);

  ROM #(.addrWidth(16), .dataWidth(16)) rom_1 ();  // open: addr, data

  // Notes on the sheet:
  //   contents of rom_1 (hex, n*v repeats v):
  //   2041 2082 20c3 2104 2145 2186 21c7 903f
endmodule

module memory_latch (
  input  [15:0] address,
  input  WE,
  input  clk,
  input  [15:0] data_in,
  output [15:0] address_latched,
  output WE_latched,
  output OE_latched,
  output [15:0] data_in_latched
);

  wire DMwe_latch_q;
  wire [15:0] addr_latch_q;

  Register #(.width(16), .trigger("falling")) addr_latch (
    .D(address), .en(WE), .clk(clk), .Q(addr_latch_q));  // open: clr
  D_Flip_Flop #(.trigger("falling")) DMwe_latch (.D(WE), .clk(clk), .Q(DMwe_latch_q));  // open: Qn, preset, reset
  Register #(.width(16), .trigger("falling")) data_to_be_written (
    .D(data_in), .en(WE), .clk(clk), .Q(data_in_latched));  // open: clr
  Multiplexer #(.width(16), .enable("false")) multiplexer_1 (
    .in0(address), .in1(addr_latch_q), .out(address_latched), .sel(DMwe_latch_q));
  and and_1 (WE_latched, clk, DMwe_latch_q);
  not not_1 (OE_latched, WE_latched);
endmodule
